# Fritzing sketch CW Explorer.RX (saved by Fritzing 0.9.4)
breadboards: 1

parts:
  Part1 = XBee Explorer Regulated
  Part2 = Arduino Nano (Rev3.0)
  U2 = Optocoupler [package=THT]
  U3 = Optocoupler [package=THT]
  LED1 = LED - 5mm [color="Red (633nm)" package="5 mm [THT]"]
  LED2 = LED - 5mm [color="Red (633nm)" package="5 mm [THT]"]
  TRS1 = Audio Jack (TRS) 3.5mm [package="PG203J [THT]"]

nets:
  GND: Part1.GND, Part2.RESET, Part2.GND
  N1: Part1.DIN, Part2.D3
  N2: Part1.DOUT, Part2.D2
  N3: Part1.DIO0, U2.Pin_2
  N4: Part1.DIO1, U3.Pin_2
  5V: Part1.5V, Part2.5V, LED1.anode, LED2.anode
  N5: U2.Pin_1, LED1.cathode
  N6: U2.Pin_4, U3.Pin_4, TRS1.Sleeve
  N7: U2.Pin_5, TRS1.Tip
  N8: U3.Pin_1, LED2.cathode
  N9: U3.Pin_5, TRS1.Ring

notes:
  Receiver

// code stored in the sketch: Software_Serial_Adapter.ino
#include <SoftwareSerial.h>

SoftwareSerial Xbee(2,3);

void setup() {
  // put your setup code here, to run once:
  Serial.begin(9600);
  Xbee.begin(9600);
}

void loop() {
  // put your main code here, to run repeatedly:
  if (Serial.available())
  { // If data comes in from serial monitor, send it out to XBee
    Xbee.write(Serial.read());
  }
  if (Xbee.available())
  { // If data comes in from XBee, send it out to serial monitor
    Serial.write(Xbee.read());
  }
}
