# Fritzing sketch CW Explorer.TX (saved by Fritzing 0.9.4)
breadboards: 1

parts:
  Part3 = XBee Explorer Regulated
  Part4 = Arduino Nano (Rev3.0)
  LED3 = LED - 5mm [color="Red (633nm)" package="5 mm [THT]"]
  LED4 = LED - 5mm [color="Red (633nm)" package="5 mm [THT]"]
  TRS2 = Audio Jack (TRS) 3.5mm [package="PG203J [THT]"]

nets:
  GND: Part3.GND, Part4.RESET, Part4.GND, TRS2.Sleeve
  N1: Part3.DIN, Part4.D1/TX
  N2: Part3.DOUT, Part4.D0/RX
  N3: Part3.DIO0, LED3.cathode
  N4: Part3.DIO1, LED4.anode
  5V: Part3.5V, Part4.5V
  N5: LED3.anode, TRS2.Tip
  N6: LED4.cathode, TRS2.Ring

notes:
  Transmitter
